// Digital circuit single_cycle_riscv_cpu.dig as structural Verilog
module single_cycle_riscv_cpu (
  output [31:0] out_1
);

  wire ALUControl, ALUSrc, Branch, clk, ImmSrc, MemWrite, PCSrc, RegWrite, Zero;
  wire [1:0] ResultSrc;
  wire [2:0] funct3;
  wire [4:0] Instruction_Memory_d, Instruction_Memory_d_2;
  wire [6:0] funct7, op;
  wire [17:13] Instruction_Memory_d_3;
  wire [31:0] add_1_s, add_2_s, Data_Memory_d, Extend_p3, multiplexer_1_out, multiplexer_2_out,
       multiplexer_3_out, PC_q, Register_File_da, Register_File_db;

  Add #(.Bits(32)) add_1 (.a(PC_q), .b(32'h1), .c_i(1'b0), .s(add_1_s));  // open: c_o
  Multiplexer #(.Bits(32)) multiplexer_1 (.sel(PCSrc), .in_0(add_1_s), .in_1(add_2_s), .out(multiplexer_1_out));
  Register #(.Bits(32), .isProgramCounter("true")) PC (.D(multiplexer_1_out), .C(clk), .en(1'b1), .Q(PC_q));
  Add #(.Bits(32)) add_2 (.a(Extend_p3), .b(PC_q), .c_i(1'b0), .s(add_2_s));  // open: c_o
  EEPROMDualPort #(.AddrBits(24), .isProgramMemory("true"), .Bits(32)) Instruction_Memory (
    .A(PC_q[23:0]), .Din({32{1'b0}}), .str(1'b0), .C(clk), .ld(1'b1),
    .D({funct7, Instruction_Memory_d_3, Instruction_Memory_d_2, funct3, Instruction_Memory_d, op}));
  Button button_1 (.out(clk));
  Multiplexer #(.Selector_Bits(2), .Bits(32)) multiplexer_2 (
    .sel(ResultSrc), .in_0(out_1), .in_1(Data_Memory_d), .in_2(add_1_s), .in_3({32{1'b0}}),
    .out(multiplexer_2_out));
  // sign_extend_unit Extend: pin names not known; wires that end beside it: {funct7, Instruction_Memory_d_3, Instruction_Memory_d_2, funct3, Instruction_Memory_d}, ImmSrc, Extend_p3
  RegisterFile #(.AddrBits(5), .Bits(32)) Register_File (
    .Din(multiplexer_2_out), .we(RegWrite), .Rw(Instruction_Memory_d), .C(clk), .Ra(Instruction_Memory_d_2),
    .Rb(Instruction_Memory_d_3), .Da(Register_File_da), .Db(Register_File_db));
  // decoder decoder_1: pin names not known; wires that end beside it: op, Zero, funct3, funct7, RegWrite, ImmSrc, ALUSrc, MemWrite, ResultSrc, Branch, PCSrc, ALUControl
  Multiplexer #(.Bits(32)) multiplexer_3 (
    .sel(ALUSrc), .in_0(Register_File_db), .in_1(Extend_p3), .out(multiplexer_3_out));
  // ALU ALU: pin names not known; wires that end beside it: Register_File_da, multiplexer_3_out, ALUControl, out_1, Zero
  EEPROMDualPort #(.AddrBits(24), .Bits(32)) Data_Memory (
    .A(out_1[23:0]), .Din(Register_File_db), .str(MemWrite), .C(clk), .ld(1'b1), .D(Data_Memory_d));

  // Notes on the sheet:
  //   # test a few programmes + find a solution to the byte addressable issue
  //   @abdalrahimnaser
  //   contents of Instruction_Memory (hex, n*v repeats v):
  //   52283,5a303,6283b3,3ae33,e0463,c0006f,762023,c0006f,762023,40006f
endmodule
